// Logisim project control_logic.circ as structural Verilog: 1 circuit, main circuit control_logic
module control_logic (
  input  [31:0] inst,
  input  BrEq,
  input  BrLt,
  output PCSel,
  output RegWEn,
  output [2:0] ImmSel,
  output BrUn,
  output ASel,
  output BSel,
  output [3:0] ALUSel,
  output MemRW,
  output [1:0] WBSel,
  output CSRSel,
  output CSRWen
);

  wire add0, addi0, and0, and_25_out, and_26_out, and_27_out, and_28_out, and_29_out, and_30_out, andi0,
       beq0, bge0, bgeu0, blt0, bltu0, bne0, BrEq_NOT, BrLt_NOT, funct3_0_NOT, funct3_1_NOT, funct3_2_NOT,
       funct7_0_NOT, funct7_5_NOT, isAUIPC, isBType, isIType, isJAL, isJALR, isLType, isLUI, isRType, mul0,
       mulh0, mulhu0, opcode_2_NOT, opcode_3_NOT, opcode_4_NOT, opcode_5_NOT, opcode_6_NOT, or0, or_1_out,
       or_3_out, or_4_out, or_6_out, or_7_out, or_9_out, or_10_out, or_11_out, or_12_out, or_13_out,
       or_14_out, or_15_out, ori0, sll0, slt0, slti0, sra0, srl0, sub0, xor0, xori0;

  and and_1 (isRType, inst[0], inst[1], opcode_2_NOT, opcode_3_NOT, inst[4], inst[5], opcode_6_NOT);
  and and_2 (isLType, inst[0], inst[1], opcode_2_NOT, opcode_3_NOT, opcode_4_NOT, opcode_5_NOT, opcode_6_NOT);
  and and_3 (isIType, inst[0], inst[1], opcode_2_NOT, opcode_3_NOT, inst[4], opcode_5_NOT, opcode_6_NOT);
  and and_4 (beq0, isBType, funct3_0_NOT, funct3_1_NOT, funct3_2_NOT);
  and and_5 (bne0, isBType, inst[12], funct3_1_NOT, funct3_2_NOT);
  and and_6 (blt0, isBType, funct3_0_NOT, funct3_1_NOT, inst[14]);
  and and_7 (bge0, isBType, inst[12], funct3_1_NOT, inst[14]);
  and and_8 (bltu0, isBType, funct3_0_NOT, inst[13], inst[14]);
  and and_9 (bgeu0, isBType, inst[12], inst[13], inst[14]);
  and and_10 (isBType, inst[0], inst[1], opcode_2_NOT, opcode_3_NOT, opcode_4_NOT, inst[5], inst[6]);
  and and_11 (isAUIPC, inst[0], inst[1], inst[2], opcode_3_NOT, inst[4], opcode_5_NOT, opcode_6_NOT);
  and and_12 (isLUI, inst[0], inst[1], inst[2], opcode_3_NOT, inst[4], inst[5], opcode_6_NOT);
  or or_1 (or_1_out, isRType, isIType);
  and and_13 (add0, funct3_0_NOT, funct3_1_NOT, funct3_2_NOT, funct7_0_NOT, funct7_5_NOT, isRType);
  and and_14 (mul0, funct3_0_NOT, funct3_1_NOT, funct3_2_NOT, inst[25], funct7_5_NOT, isRType);
  and and_15 (sub0, funct3_0_NOT, funct3_1_NOT, funct3_2_NOT, funct7_0_NOT, inst[30], isRType);
  and and_16 (sll0, inst[12], funct3_1_NOT, funct3_2_NOT, funct7_0_NOT, funct7_5_NOT, or_1_out);
  not not_1 (opcode_2_NOT, inst[2]);
  not not_2 (opcode_3_NOT, inst[3]);
  not not_3 (opcode_4_NOT, inst[4]);
  not not_4 (opcode_5_NOT, inst[5]);
  not not_5 (opcode_6_NOT, inst[6]);
  and and_17 (isJALR, inst[0], inst[1], inst[2], opcode_3_NOT, opcode_4_NOT, inst[5], inst[6]);
  and and_18 (CSRWen, inst[0], inst[1], opcode_2_NOT, opcode_3_NOT, inst[4], inst[5], inst[6]);
  and and_19 (MemRW, inst[0], inst[1], opcode_2_NOT, opcode_3_NOT, opcode_4_NOT, inst[5], opcode_6_NOT);
  and and_20 (addi0, funct3_0_NOT, funct3_1_NOT, funct3_2_NOT, isIType);
  and and_21 (slti0, funct3_0_NOT, inst[13], funct3_2_NOT, isIType);
  and and_22 (xori0, funct3_0_NOT, funct3_1_NOT, inst[14], isIType);
  and and_23 (ori0, funct3_0_NOT, inst[13], inst[14], isIType);
  and and_24 (andi0, inst[12], inst[13], inst[14], isIType);
  and and_25 (and_25_out, beq0, BrEq);
  and and_26 (and_26_out, bne0, BrEq_NOT);
  and and_27 (and_27_out, blt0, BrLt);
  and and_28 (and_28_out, bge0, BrLt_NOT);
  and and_29 (and_29_out, bltu0, BrLt);
  and and_30 (and_30_out, bgeu0, BrLt_NOT);
  not not_6 (funct3_0_NOT, inst[12]);
  not not_7 (funct3_1_NOT, inst[13]);
  not not_8 (funct3_2_NOT, inst[14]);
  not not_9 (funct7_0_NOT, inst[25]);
  not not_10 (funct7_5_NOT, inst[30]);
  not not_11 (BrEq_NOT, BrEq);
  not not_12 (BrLt_NOT, BrLt);
  or or_2 (PCSel, and_25_out, and_26_out, and_27_out, and_28_out, and_29_out, and_30_out, isJAL, isJALR);
  and and_31 (mulh0, inst[12], funct3_1_NOT, funct3_2_NOT, inst[25], funct7_5_NOT, isRType);
  and and_32 (mulhu0, inst[12], inst[13], funct3_2_NOT, inst[25], funct7_5_NOT, isRType);
  and and_33 (slt0, funct3_0_NOT, inst[13], funct3_2_NOT, funct7_0_NOT, funct7_5_NOT, isRType);
  and and_34 (xor0, funct3_0_NOT, funct3_1_NOT, inst[14], funct7_0_NOT, funct7_5_NOT, isRType);
  and and_35 (isJAL, inst[0], inst[1], inst[2], inst[3], opcode_4_NOT, inst[5], inst[6]);
  and and_36 (RegWEn, ~MemRW, ~isBType);  // AND_Gate
  or or_3 (or_3_out, isIType, isJALR, isLType);
  or or_4 (or_4_out, isAUIPC, isLUI);
  or or_5 (BrUn, bltu0, bgeu0);
  Priority_Encoder priority_encoder_1 (
    .in0(isRType), .in1(or_3_out), .in2(MemRW), .in3(isBType), .in4(or_4_out), .in5(isJAL), .in6(1'b0),
    .in7(1'b0), .out(ImmSel));  // open: en_in, gs, en_out
  or or_6 (or_6_out, isRType, isIType);
  or or_7 (or_7_out, isRType, isIType);
  not not_13 (BSel, isRType);
  and and_37 (srl0, inst[12], funct3_1_NOT, inst[14], funct7_0_NOT, funct7_5_NOT, or_6_out);
  and and_38 (sra0, inst[12], funct3_1_NOT, inst[14], funct7_0_NOT, inst[30], or_7_out);
  and and_39 (or0, funct3_0_NOT, inst[13], inst[14], funct7_0_NOT, funct7_5_NOT, isRType);
  and and_40 (and0, inst[12], inst[13], inst[14], funct7_0_NOT, funct7_5_NOT, isRType);
  or or_8 (ASel, isBType, isJAL, isAUIPC);
  or or_9 (or_9_out, isRType, isIType, isAUIPC, isLUI);
  or or_10 (or_10_out, isJAL, isJALR);
  Priority_Encoder #(.select(2)) priority_encoder_2 (
    .in0(isLType), .in1(or_9_out), .in2(or_10_out), .in3(1'b0), .out(WBSel));  // open: gs, en_out, en_in
  and and_41 (CSRSel, CSRWen, inst[14]);
  or or_11 (or_11_out, add0, addi0, MemRW, isLType, isBType, isAUIPC, isJAL, isJALR);
  or or_12 (or_12_out, and0, andi0);
  or or_13 (or_13_out, or0, ori0);
  or or_14 (or_14_out, xor0, xori0);
  or or_15 (or_15_out, slt0, slti0);
  Priority_Encoder #(.select(4)) priority_encoder_3 (
    .in0(or_11_out), .in1(or_12_out), .in2(or_13_out), .in3(or_14_out), .in4(srl0), .in5(sra0), .in6(sll0),
    .in7(or_15_out), .in8(1'b0), .in9(1'b0), .in10(mul0), .in11(mulhu0), .in12(sub0), .in13(isLUI),
    .in14(mulh0), .in15(1'b0), .out(ALUSel));  // open: gs, en_out, en_in

  // Other names for the same wires on the sheet: opcode[6:0] = inst[6:0]; opcode_0 = inst[0]; opcode_1 = inst[1];
  //   opcode_2 = inst[2]; opcode_3 = inst[3]; opcode_4 = inst[4]; opcode_5 = inst[5]; opcode_6 = inst[6];
  //   rd[4:0] = inst[11:7]; funct3[2:0] = inst[14:12]; funct3_0 = inst[12]; funct3_1 = inst[13]; funct3_2 = inst[14];
  //   rs1[4:0] = inst[19:15]; rs2[4:0] = inst[24:20]; funct7[6:0] = inst[31:25]; funct7_0 = inst[25];
  //   funct7_5 = inst[30]; isCSRType = CSRWen; isSType = MemRW

  // Notes on the sheet:
  //   INPUTS to your circuit
  //   DON'T CHANGE THE LOCATIONS OF THE INPUTS AND OUTPUTS!
  //   OUTPUT from your circuit
endmodule
