// Logisim project cpu.circ as structural Verilog: 1 circuit, main circuit cpu
module cpu (
  input  clk,
  input  [31:0] INSTRUCTION,
  input  [31:0] READ_DATA,
  output [31:0] WRITE_ADDRESS,
  output [31:0] PROGRAM_COUNTER,
  output [31:0] ra,
  output [31:0] sp,
  output [31:0] t0,
  output [31:0] t1,
  output [31:0] t2,
  output [31:0] s0,
  output [31:0] s1,
  output [31:0] a0,
  output [31:0] tohost,
  output [3:0] WRITE_ENABLE,
  output [31:0] WRITE_DATA
);

  wire ASel, BrEq, BrLt, BrUn, BSel, CSRSel, CSRWen, MemRW, PCSel, RegWEn;
  wire [1:0] ALU_Out, WBSel;
  wire [2:0] funct3, ImmSel;
  wire [3:0] ALUSel, multiplexer_1_out, shifter_1_out;
  wire [6:0] shifter_3_out, shifter_3_out_3;
  wire [31:0] adder_2_out, imm_gen_1_imm, INST_Fetched, multiplexer_2_out, multiplexer_3_out,
       multiplexer_4_out, multiplexer_5_out, multiplexer_6_out, multiplexer_7_out, PC_PIPELINED, PC_PLUS_4,
       Read_Data_1, Read_Data_2, READ_DATA_MASKED;
  wire [31:16] shifter_3_out_5;
  wire [31:31] shifter_3_out_2, shifter_3_out_4;

  Multiplexer #(.enable("false"), .select(2), .width(4)) multiplexer_1 (
    .in0(4'b0001), .in1(4'b0011), .in2(4'b1111), .in3(4'b0000), .out(multiplexer_1_out), .sel(funct3[1:0]));
  Adder #(.width(32)) adder_1 (.a(PROGRAM_COUNTER), .b(32'h4), .out(PC_PLUS_4));  // open: cin, cout
  Register #(.width(32)) PC (.D(multiplexer_2_out), .clk(clk), .Q(PROGRAM_COUNTER));  // open: en, clr
  Multiplexer #(.enable("false"), .width(32)) multiplexer_2 (
    .in0(PC_PLUS_4), .in1({WRITE_ADDRESS[31:2], ALU_Out}), .out(multiplexer_2_out), .sel(PCSel));
  Multiplexer #(.enable("false"), .width(32)) multiplexer_3 (
    .in0(INSTRUCTION), .in1(32'h13), .out(multiplexer_3_out), .sel(PCSel));
  Register #(.width(32)) register_1 (
    .D(multiplexer_3_out), .clk(clk), .Q({INST_Fetched[31:15], funct3, INST_Fetched[11:0]}));  // open: en, clr
  Shifter #(.width(4)) shifter_1 (.in(multiplexer_1_out), .\dist (ALU_Out), .out(shifter_1_out));
  Register #(.width(32)) register_2 (.D(PROGRAM_COUNTER), .clk(clk), .Q(PC_PIPELINED));  // open: en, clr
  assign WRITE_ENABLE = shifter_1_out & {4{MemRW}};  // AND_Gate and_1, 4 bits wide
  control_logic control_logic_1 (
    .CSRWen(CSRWen), .PCSel(PCSel), .RegWEn(RegWEn), .ImmSel(ImmSel), .BrUn(BrUn), .ASel(ASel), .BSel(BSel),
    .ALUSel(ALUSel), .MemRW(MemRW), .WBSel(WBSel), .CSRSel(CSRSel),
    .inst({INST_Fetched[31:15], funct3, INST_Fetched[11:0]}), .BrEq(BrEq), .BrLt(BrLt));
  regfile regfile_1 (
    .rs1(INST_Fetched[19:15]), .rs2(INST_Fetched[24:20]), .rd(INST_Fetched[11:7]),
    .Write_Data(multiplexer_7_out), .RegWEn(RegWEn), .clk(clk), .ra(ra), .sp(sp), .t0(t0), .t1(t1), .t2(t2),
    .s0(s0), .s1(s1), .a0(a0), .Read_Data_1(Read_Data_1), .Read_Data_2(Read_Data_2));
  imm_gen imm_gen_1 (.inst({INST_Fetched[31:15], funct3, INST_Fetched[11:0]}), .ImmSel(ImmSel), .imm(imm_gen_1_imm));
  branch_comp branch_comp_1 (.rs1(Read_Data_1), .rs2(Read_Data_2), .BrUn(BrUn), .BrEq(BrEq), .BrLt(BrLt));
  Multiplexer #(.enable("false"), .width(32)) multiplexer_4 (
    .in0(Read_Data_1), .in1(PC_PIPELINED), .out(multiplexer_4_out), .sel(ASel));
  Multiplexer #(.enable("false"), .width(32)) multiplexer_5 (
    .in0(Read_Data_2), .in1(imm_gen_1_imm), .out(multiplexer_5_out), .sel(BSel));
  Multiplexer #(.enable("false"), .width(32)) multiplexer_6 (
    .in0(Read_Data_1), .in1({{27{1'b0}}, INST_Fetched[19:15]}), .out(multiplexer_6_out), .sel(CSRSel));
  alu alu_1 (.Result({WRITE_ADDRESS[31:2], ALU_Out}), .A(multiplexer_4_out), .B(multiplexer_5_out), .ALUSel(ALUSel));
  Shifter #(.width(32)) shifter_2 (.in(Read_Data_2), .\dist ({ALU_Out, 3'b000}), .out(WRITE_DATA));
  csr csr_1 (
    .CSR_address(INST_Fetched[31:20]), .CSR_din(multiplexer_6_out), .CSR_WE(CSRWen), .clk(clk),
    .tohost(tohost));
  Multiplexer #(.enable("false"), .select(2), .width(32)) multiplexer_7 (
    .in0(READ_DATA_MASKED), .in1({WRITE_ADDRESS[31:2], ALU_Out}), .in2(adder_2_out), .out(multiplexer_7_out),
    .sel(WBSel));  // open: in3
  Adder #(.width(32)) adder_2 (.a(32'h4), .b(PC_PIPELINED), .out(adder_2_out));  // open: cin, cout
  Shifter #(.shift("lr"), .width(32)) shifter_3 (
    .in(READ_DATA), .\dist ({ALU_Out, 3'b000}),
    .out({shifter_3_out_5, shifter_3_out_4[31], shifter_3_out_3, shifter_3_out_2[31], shifter_3_out}));
  Multiplexer #(.enable("false"), .select(2), .width(32)) multiplexer_8 (
    .in0({{25{shifter_3_out_2[31]}}, shifter_3_out}),
    .in1({{17{shifter_3_out_4[31]}}, shifter_3_out_3, shifter_3_out_2[31], shifter_3_out}),
    .in2({shifter_3_out_5, shifter_3_out_4[31], shifter_3_out_3, shifter_3_out_2[31], shifter_3_out}),
    .out(READ_DATA_MASKED), .sel(funct3[1:0]));  // open: in3

  assign WRITE_ADDRESS[1:0] = 2'b00;

  // Other names for the same wires on the sheet: rs1[4:0] = INST_Fetched[19:15]; Byte_Offset[4:3] = ALU_Out;
  //   INST[31:0] = INSTRUCTION; rd[4:0] = INST_Fetched[11:7]; INST_Fetched[14:12] = funct3;
  //   rs2[4:0] = INST_Fetched[24:20]; ALU_Out[31:2] = WRITE_ADDRESS[31:2]

  // Notes on the sheet:
  //   Output to IMEM
  //   IMEM (do **NOT** move this)
  //   Inputs from IMEM
  //   PIPELINED_INSTRUCTION
  //   It is OK to move the PC, RegFile, ALU, MEM, Branch Comp, Imm Gen, and Control Logic to wherever is most convenient for you when constructing your CPU
  //   Inputs/Outputs for testing. Do **NOT** move these.
  //   Outputs To DMEM
  //   DMEM (do **NOT** move this)
  //   Inputs From DMEM
endmodule
