// Logisim project imm_gen.circ as structural Verilog: 1 circuit, main circuit imm_gen
module imm_gen (
  input  [31:0] inst,
  input  [2:0] ImmSel,
  output [31:0] imm
);

  wire [11:0] demultiplexer_1_out4;
  wire [31:0] B_Type, demultiplexer_1_out1, demultiplexer_1_out2, demultiplexer_1_out3, demultiplexer_1_out5,
       I_Type, J_Type, S_Type;
  wire [31:12] U_Type;

  Demultiplexer #(.enable("false"), .select(3), .width(32)) demultiplexer_1 (
    .out1(demultiplexer_1_out1), .out2(demultiplexer_1_out2), .out3(demultiplexer_1_out3),
    .out4({U_Type, demultiplexer_1_out4}), .out5(demultiplexer_1_out5), .in(inst), .sel(ImmSel));  // open: out0, out6, out7
  assign I_Type = {{20{demultiplexer_1_out1[31]}}, demultiplexer_1_out1[31:20]};  // Bit_Extender bit_extender_1
  assign S_Type = {{20{demultiplexer_1_out2[31]}}, {demultiplexer_1_out2[31:25], demultiplexer_1_out2[11:7]}};  // Bit_Extender bit_extender_2
  assign B_Type = {{19{demultiplexer_1_out3[31]}}, {demultiplexer_1_out3[31], demultiplexer_1_out3[7], demultiplexer_1_out3[30:25], demultiplexer_1_out3[11:8], 1'b0}};  // Bit_Extender bit_extender_3
  assign J_Type = {{11{demultiplexer_1_out5[31]}}, {demultiplexer_1_out5[31], demultiplexer_1_out5[19:12], demultiplexer_1_out5[20], demultiplexer_1_out5[30:21], 1'b0}};  // Bit_Extender bit_extender_4
  Multiplexer #(.enable("false"), .select(3), .width(32)) multiplexer_1 (
    .in1(I_Type), .in2(S_Type), .in3(B_Type), .in4({U_Type, {12{1'b0}}}), .in5(J_Type), .out(imm),
    .sel(ImmSel));  // open: in0, in6, in7

  // Notes on the sheet:
  //   INPUTS to your circuit
  //   DON'T CHANGE THE LOCATIONS OF THE INPUTS AND OUTPUTS!
  //   OUTPUT from your circuit
endmodule
