// Logisim project regfile.circ as structural Verilog: 1 circuit, main circuit regfile
module regfile (
  input  [4:0] rs1,
  input  [4:0] rs2,
  input  [4:0] rd,
  input  [31:0] Write_Data,
  input  RegWEn,
  input  clk,
  output [31:0] ra,
  output [31:0] sp,
  output [31:0] t0,
  output [31:0] t1,
  output [31:0] t2,
  output [31:0] s0,
  output [31:0] s1,
  output [31:0] a0,
  output [31:0] Read_Data_1,
  output [31:0] Read_Data_2
);

  wire reg1_we, reg2_we, reg3_we, reg4_we, reg5_we, reg6_we, reg7_we, reg8_we, reg9_we, reg10_we, reg11_we,
       reg12_we, reg13_we, reg14_we, reg15_we, reg16_we, reg17_we, reg18_we, reg19_we, reg20_we, reg21_we,
       reg22_we, reg23_we, reg24_we, reg25_we, reg26_we, reg27_we, reg28_we, reg29_we, reg30_we, reg31_we;
  wire [31:0] reg0_out, reg3_out, reg4_out, reg11_out, reg12_out, reg13_out, reg14_out, reg15_out, reg16_out,
       reg17_out, reg18_out, reg19_out, reg20_out, reg21_out, reg22_out, reg23_out, reg24_out, reg25_out,
       reg26_out, reg27_out, reg28_out, reg29_out, reg30_out, reg31_out;

  Register #(.width(32)) x0 (.Q(reg0_out));  // open: D, en, clk, clr
  Register #(.width(32)) register_1 (.D(Write_Data), .en(reg1_we), .clk(clk), .Q(ra));  // open: clr
  Register #(.width(32)) register_2 (.D(Write_Data), .en(reg2_we), .clk(clk), .Q(sp));  // open: clr
  Register #(.width(32)) register_3 (.D(Write_Data), .en(reg3_we), .clk(clk), .Q(reg3_out));  // open: clr
  Register #(.width(32)) register_4 (.D(Write_Data), .en(reg4_we), .clk(clk), .Q(reg4_out));  // open: clr
  Register #(.width(32)) register_5 (.D(Write_Data), .en(reg5_we), .clk(clk), .Q(t0));  // open: clr
  Register #(.width(32)) register_6 (.D(Write_Data), .en(reg6_we), .clk(clk), .Q(t1));  // open: clr
  Register #(.width(32)) register_7 (.D(Write_Data), .en(reg7_we), .clk(clk), .Q(t2));  // open: clr
  Register #(.width(32)) register_8 (.D(Write_Data), .en(reg8_we), .clk(clk), .Q(s0));  // open: clr
  Register #(.width(32)) register_9 (.D(Write_Data), .en(reg9_we), .clk(clk), .Q(s1));  // open: clr
  Register #(.width(32)) register_10 (.D(Write_Data), .en(reg10_we), .clk(clk), .Q(a0));  // open: clr
  Register #(.width(32)) register_11 (.D(Write_Data), .en(reg11_we), .clk(clk), .Q(reg11_out));  // open: clr
  Register #(.width(32)) register_12 (.D(Write_Data), .en(reg12_we), .clk(clk), .Q(reg12_out));  // open: clr
  Register #(.width(32)) register_13 (.D(Write_Data), .en(reg13_we), .clk(clk), .Q(reg13_out));  // open: clr
  Register #(.width(32)) register_14 (.D(Write_Data), .en(reg14_we), .clk(clk), .Q(reg14_out));  // open: clr
  Register #(.width(32)) register_15 (.D(Write_Data), .en(reg15_we), .clk(clk), .Q(reg15_out));  // open: clr
  Register #(.width(32)) register_16 (.D(Write_Data), .en(reg16_we), .clk(clk), .Q(reg16_out));  // open: clr
  Register #(.width(32)) register_17 (.D(Write_Data), .en(reg17_we), .clk(clk), .Q(reg17_out));  // open: clr
  Register #(.width(32)) register_18 (.D(Write_Data), .en(reg18_we), .clk(clk), .Q(reg18_out));  // open: clr
  Register #(.width(32)) register_19 (.D(Write_Data), .en(reg19_we), .clk(clk), .Q(reg19_out));  // open: clr
  Register #(.width(32)) register_20 (.D(Write_Data), .en(reg20_we), .clk(clk), .Q(reg20_out));  // open: clr
  Register #(.width(32)) register_21 (.D(Write_Data), .en(reg21_we), .clk(clk), .Q(reg21_out));  // open: clr
  Register #(.width(32)) register_22 (.D(Write_Data), .en(reg22_we), .clk(clk), .Q(reg22_out));  // open: clr
  Register #(.width(32)) register_23 (.D(Write_Data), .en(reg23_we), .clk(clk), .Q(reg23_out));  // open: clr
  Register #(.width(32)) register_24 (.D(Write_Data), .en(reg24_we), .clk(clk), .Q(reg24_out));  // open: clr
  Register #(.width(32)) register_25 (.D(Write_Data), .en(reg25_we), .clk(clk), .Q(reg25_out));  // open: clr
  Register #(.width(32)) register_26 (.D(Write_Data), .en(reg26_we), .clk(clk), .Q(reg26_out));  // open: clr
  Register #(.width(32)) register_27 (.D(Write_Data), .en(reg27_we), .clk(clk), .Q(reg27_out));  // open: clr
  Register #(.width(32)) register_28 (.D(Write_Data), .en(reg28_we), .clk(clk), .Q(reg28_out));  // open: clr
  Register #(.width(32)) register_29 (.D(Write_Data), .en(reg29_we), .clk(clk), .Q(reg29_out));  // open: clr
  Register #(.width(32)) register_30 (.D(Write_Data), .en(reg30_we), .clk(clk), .Q(reg30_out));  // open: clr
  Register #(.width(32)) register_31 (.D(Write_Data), .en(reg31_we), .clk(clk), .Q(reg31_out));  // open: clr
  Demultiplexer #(.enable("false"), .select(5)) demultiplexer_1 (
    .out1(reg1_we), .out2(reg2_we), .out3(reg3_we), .out4(reg4_we), .out5(reg5_we), .out6(reg6_we),
    .out7(reg7_we), .out8(reg8_we), .out9(reg9_we), .out10(reg10_we), .out11(reg11_we), .out12(reg12_we),
    .out13(reg13_we), .out14(reg14_we), .out15(reg15_we), .out16(reg16_we), .out17(reg17_we),
    .out18(reg18_we), .out19(reg19_we), .out20(reg20_we), .out21(reg21_we), .out22(reg22_we),
    .out23(reg23_we), .out24(reg24_we), .out25(reg25_we), .out26(reg26_we), .out27(reg27_we),
    .out28(reg28_we), .out29(reg29_we), .out30(reg30_we), .out31(reg31_we), .in(RegWEn), .sel(rd));  // open: out0
  Multiplexer #(.enable("false"), .select(5), .width(32)) multiplexer_1 (
    .in0(reg0_out), .in1(ra), .in2(sp), .in3(reg3_out), .in4(reg4_out), .in5(t0), .in6(t1), .in7(t2),
    .in8(s0), .in9(s1), .in10(a0), .in11(reg11_out), .in12(reg12_out), .in13(reg13_out), .in14(reg14_out),
    .in15(reg15_out), .in16(reg16_out), .in17(reg17_out), .in18(reg18_out), .in19(reg19_out),
    .in20(reg20_out), .in21(reg21_out), .in22(reg22_out), .in23(reg23_out), .in24(reg24_out),
    .in25(reg25_out), .in26(reg26_out), .in27(reg27_out), .in28(reg28_out), .in29(reg29_out),
    .in30(reg30_out), .in31(reg31_out), .out(Read_Data_1), .sel(rs1));
  Multiplexer #(.enable("false"), .select(5), .width(32)) multiplexer_2 (
    .in0(reg0_out), .in1(ra), .in2(sp), .in3(reg3_out), .in4(reg4_out), .in5(t0), .in6(t1), .in7(t2),
    .in8(s0), .in9(s1), .in10(a0), .in11(reg11_out), .in12(reg12_out), .in13(reg13_out), .in14(reg14_out),
    .in15(reg15_out), .in16(reg16_out), .in17(reg17_out), .in18(reg18_out), .in19(reg19_out),
    .in20(reg20_out), .in21(reg21_out), .in22(reg22_out), .in23(reg23_out), .in24(reg24_out),
    .in25(reg25_out), .in26(reg26_out), .in27(reg27_out), .in28(reg28_out), .in29(reg29_out),
    .in30(reg30_out), .in31(reg31_out), .out(Read_Data_2), .sel(rs2));

  // Other names for the same wires on the sheet: read_data1[31:0] = Read_Data_1; read_data2[31:0] = Read_Data_2;
  //   read_reg1[4:0] = rs1; read_reg2[4:0] = rs2; reg1_out[31:0] = ra; reg2_out[31:0] = sp; reg5_out[31:0] = t0;
  //   reg6_out[31:0] = t1; reg7_out[31:0] = t2; reg8_out[31:0] = s0; reg9_out[31:0] = s1; reg10_out[31:0] = a0;
  //   write_en = RegWEn; write_reg[4:0] = rd

  // Notes on the sheet:
  //   INPUTS to your circuit
  //   DON'T CHANGE THE LOCATIONS OF THE INPUTS AND OUTPUTS!
  //   These are DEBUG/TEST outputs from your circuit.
  //   OUTPUTS from your circuit
endmodule
