// Logisim project cpu-memory2.circ as structural Verilog: 1 circuit, main circuit run_main
module run_main (
  output [31:0] ra,
  output [31:0] sp,
  output [31:0] t0,
  output [31:0] t1,
  output [31:0] t2,
  output [31:0] s0,
  output [31:0] s1,
  output [31:0] a0,
  output [31:0] Requested_Address,
  output [31:0] Requested_Instruction,
  output [15:0] Time_Step,
  output halt
);

  wire clk;

  Clock clock_1 (.out(clk));
  // Probe on Requested_Address
  // test_harness test_harness_1: pin names not known; wires that end beside it: Requested_Instruction, clk, Requested_Address, ra, sp, t0, t1, t2, s0, s1, a0
  ROM #(.addrWidth(14), .dataWidth(32)) rom_1 (.addr(Requested_Address[15:2]), .data(Requested_Instruction));
  // Probe on Requested_Instruction
  Counter #(.max('hffff), .width(16)) counter_1 (.clk(clk), .Q(Time_Step));  // open: clr, load, up, count, D, carry
  Comparator #(.width(16)) comparator_1 (.a(Time_Step), .b(16'h69), .eq(halt));  // open: gt, lt

  // Other names for the same wires on the sheet: fetch_addr[31:0] = Requested_Address;
  //   Instruction[31:0] = Requested_Instruction

  // Notes on the sheet:
  //   contents of rom_1 (hex, n*v repeats v):
  //   0FF00C93 00100293 00010433 0F000D13 019D00A3 005C8CB3 019D0023 005C8CB3 019D00A3 005C8CB3 019D0123
  //   005C8CB3 019D01A3 005C8CB3 019D0223 000D0903 001D0983 002D0903 003D0983 004D0983 064C8C93 005C8CB3
  //   019D0223 004D1A03 005C8CB3 019D0423 008D1A03 11800D13 008C9C13 005C8CB3 019D1023 000D1B83 11800D13
  //   0FF00313 005C8CB3 019D2423 005C8CB3 019D2623 005C8CB3 019D2823 008D2303 00CD2383 010D2E03 019C6BB3
  //   010B9B13 017B6AB3 004D2403 006D1483 007D0903 008D0983 01248533 FF600293 3E800313 00000F17 00128293
  //   0002D663 000F0067 014A0533 014A0533
  //   Instruction Memory
  //   Halts Execution After Constant # of Clock Cycles
  //   Constant
endmodule
