// Logisim project cpu-sbtype.circ as structural Verilog: 1 circuit, main circuit run_main
module run_main (
  output [31:0] ra,
  output [31:0] sp,
  output [31:0] t0,
  output [31:0] t1,
  output [31:0] t2,
  output [31:0] s0,
  output [31:0] s1,
  output [31:0] a0,
  output [31:0] Requested_Address,
  output [31:0] Requested_Instruction,
  output [15:0] Time_Step,
  output halt
);

  wire clk;

  Clock clock_1 (.out(clk));
  // Probe on Requested_Address
  // test_harness test_harness_1: pin names not known; wires that end beside it: Requested_Instruction, clk, Requested_Address, ra, sp, t0, t1, t2, s0, s1, a0
  ROM #(.addrWidth(14), .dataWidth(32)) rom_1 (.addr(Requested_Address[15:2]), .data(Requested_Instruction));
  // Probe on Requested_Instruction
  Counter #(.max('hffff), .width(16)) counter_1 (.clk(clk), .Q(Time_Step));  // open: clr, load, up, count, D, carry
  Comparator #(.width(16)) comparator_1 (.a(Time_Step), .b(16'h63), .eq(halt));  // open: gt, lt

  // Other names for the same wires on the sheet: fetch_addr[31:0] = Requested_Address;
  //   Instruction[31:0] = Requested_Instruction

  // Notes on the sheet:
  //   contents of rom_1 (hex, n*v repeats v):
  //   000000B7 FFFFF137 00208C63 00110A63 02210033 402000B3 401000B3 00208863 00217133 002101B3 00210863
  //   FFFFF137 00008133 FE2086E3 000000B7 FFFFF137 002001B3 00311A63 00211863 02210033 401000B3 00209A63
  //   00217133 002101B3 FFF18193 00211863 FFFFF137 00008133 FE2014E3 000000B7 FFFFF137 002001B3 00314E63
  //   00214C63 02210033 401000B3 000010B7 00114C63 0020CA63 00217133 002101B3 FFF18213 00324863 FFFFF137
  //   00008133 FE2044E3 000020B7 FFFFF137 0020DE63 00100213 00225A63 02210033 401000B3 000010B7 00215A63
  //   00217133 002101B3 FFF18213 0041D863 FFFFF137 000011B7 FE3154E3 000000B7 FFFFF137 002001B3 00316E63
  //   00216C63 02210033 401000B3 000010B7 00116C63 0020EA63 00217133 002101B3 FFF18213 00326863 FFFFF137
  //   00008133 FE2064E3 000020B7 FFFFF137 0020FE63 00100213 00227A63 02210033 401000B3 000010B7 00217A63
  //   00217133 002101B3 FFF18213 0041F863 FFFFF137 000011B7 FE3174E3
  //   Instruction Memory
  //   Halts Execution After Constant # of Clock Cycles
  //   Constant
endmodule
